# Fritzing sketch Wiring Diagram (saved by Fritzing 1.0.2b)
breadboards: 1

parts:
  M2 = MH Sensor Series 4-pin IR Sensor/Line follower [package=THT]
  M4 = gear-motor-encoder-magnet
  M1 = MH Sensor Series 4-pin IR Sensor/Line follower [package=THT]
  M3 = gear-motor-encoder-magnet
  IC1 = L293D [package=THT]
  HC-SR04_Sensor_1 = HC-SR04 Ultrasonic Distance Sensor
  A1 = Arduino UNO R4 WiFi
  BAT1 = 6xAA battery  # not connected

nets:
  N1: M2.pin2, A1.Pin_41
  N2: M2.pin3, M1.pin3, IC1.0V, HC-SR04_Sensor_1.GND, A1.Pin_9, A1.Pin_30
  N3: M2.pin4, M1.pin4, IC1.+V, HC-SR04_Sensor_1.VCC, A1.Pin_8, A1.Pin_27
  N4: M4.pin_1, IC1.Out_3_(_Controlled_by_Enable_2_)
  N5: M4.pin_2, IC1.Out_4_(_Controlled_by_Enable_2_)
  N6: M1.pin2, A1.Pin_42
  N7: M3.pin_1, IC1.Out_1_(_Controlled_by_Enable_1_)
  N8: M3.pin_2, IC1.Out_2_(_Controlled_by_Enable_1_)
  N9: IC1.Enable_1, A1.Pin_45
  N10: IC1.In_1, A1.Pin_47
  N11: IC1.In_2, A1.Pin_46
  N12: IC1.+Vmotor, A1.Pin_11
  N13: IC1.Enable_2, A1.Pin_44
  N14: IC1.In_3, A1.Pin_39
  N15: IC1.In_4, A1.Pin_40
  N16: HC-SR04_Sensor_1.TRIG, A1.Pin_38
  N17: HC-SR04_Sensor_1.ECHO, A1.Pin_36

custom parts:
  MH Sensor Series 4-pin IR Sensor/Line follower: modified version of FC-51 from Peter Van Epp (vanepp in forums) This is the 4-pin version of IR line follower module, using the TCRT5000 sensor and LM393 comparator This one has the analogue output pin, in addition to the Digital pin which is set by the trimmer. The Analog pin can feed an Arduino ADC input, for much better level sensing options and less drift than the crappy potentiometer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
  gear-motor-encoder-magnet: Generic gear motor, 3V to 6V, dual output shafts, 1:48 gear ratio with magnet for wheel encoder
  Arduino UNO R4 WiFi: The Arduino UNO R4 WiFi merges the RA4M1 microprocessor from Renesas with the ESP32-S3 from Espressif, creating an all-in-one tool for makers with enhanced processing power and a diverse array of new peripherals.
